# Fritzing sketch Full_schematic (saved by Fritzing 0.9.2b)
circuit board: 20.4709cm x 12.4929cm
breadboards: 1

parts:
  LCD1 = LCD screen
  R1 = Resistor [tolerance=±5% resistance=1k package=THT]
  R2 = Resistor [tolerance=±5% resistance=4.7k package=THT]
  R3 = Resistor [tolerance=±5% resistance=10k package=THT]
  R4 = Resistor [tolerance=±5% resistance=47k package=THT]
  R5 = Resistor [tolerance=±5% resistance=100k package=THT]
  R6 = Resistor [tolerance=±5% resistance=220 package=THT]
  R7 = Resistor [tolerance=±5% resistance=10k package=THT]
  R9 = Rotary Potentiometer (Small) [maximum_resistance=100kΩ package=THT]
  S1 = Pushbutton [package="[THT]"]
  R10 = Resistor [tolerance=±5% resistance=220 package=THT]
  R11 = Resistor [tolerance=±5% resistance=10k package=THT]
  R8 = Resistor [tolerance=±5% resistance=10k package=THT]
  Part2 = Arduino Nano (Rev3.0)
  J1 = Piezo Speaker
  ZS-042_RTC1 = ZS-042 RTC Module

nets:
  GND: LCD1.VSS, LCD1.R/W, R9.leg1, R11.Pin_1, Part2.GND, ZS-042_RTC1.GND
  VDD: LCD1.VDD, R9.leg2, S1.Pin_3, S1.Pin_4, R8.Pin_0, J1.pin2, ZS-042_RTC1.VCC
  N1: LCD1.V0, R9.wiper
  N2: LCD1.RS, Part2.D1/TX
  N3: LCD1.E, Part2.D0/RX
  N4: LCD1.DB4, R7.Pin_1, Part2.D7
  N5: LCD1.DB5, Part2.D8
  N6: LCD1.DB6, Part2.D9
  N7: LCD1.DB7, Part2.D10
  N8: R1.Pin_1, R2.Pin_1, R3.Pin_1, R4.Pin_1, R5.Pin_1, Part2.A7
  N9: R2.Pin_0, Part2.D3
  N10: R3.Pin_0, Part2.D4
  N11: R4.Pin_0, Part2.D5
  N12: R5.Pin_0, Part2.D6
  N13: R6.Pin_0, Part2.D12/MISO
  N14: R6.Pin_1, R7.Pin_0, Part2.A0
  N15: S1.Pin_1, S1.Pin_2, R10.Pin_0, R11.Pin_0
  N16: R8.Pin_1, Part2.A6
  N17: Part2.A5, ZS-042_RTC1.SCL
  N18: Part2.A4, ZS-042_RTC1.SDA
  N19: Part2.A1, J1.pin1

notes:
  Resistor test here
  (+) Diode test here (- )
  (- )Capacitance test(+)
